// Logisim project brainfuck_machine.circ as structural Verilog: 6 circuits, main circuit main
module main (
  input  RESET
);

  wire and_1_out, and_2_out, and_3_out, and_4_out, and_5_out, clock_1_out, clock_2_out, clock_3_out,
       clock_4_out, clock_5_out, control_unit_1_backward, control_unit_1_count, control_unit_1_direction,
       control_unit_1_forward, control_unit_1_print, control_unit_1_write, d_ff_1_q, ENABLE_q,
       jump_unit_1_jump, jump_unit_1_override, keyboard_1_avail, not_1_out, not_2_out, not_3_out, not_4_out,
       not_5_out, or_1_out, or_2_out;
  wire [1:0] control_unit_1_read;
  wire [6:0] demultiplexer_1_out0, demultiplexer_1_out1, keyboard_1_data, register_2_q;
  wire [7:0] control_unit_1_char_out, control_unit_1_data_out, controlled_buffer_2_out,
       memory_unit_1_data_out, program_storage_1_data, register_1_q;
  wire [14:0] jump_unit_1_addr_out, program_storage_1_addr_out;

  D_Flip_Flop ENABLE (.D(1'b1), .clk(clock_1_out), .Q(ENABLE_q), .reset(RESET));  // open: Qn, preset
  Clock clock_1 (.out(clock_1_out));
  not not_1 (not_1_out, jump_unit_1_override);
  and and_1 (and_1_out, ENABLE_q, not_1_out, or_2_out);
  Clock clock_2 (.out(clock_2_out));
  or or_1 (or_1_out, jump_unit_1_override, and_1_out);
  and and_2 (and_2_out, and_1_out, control_unit_1_print, ~clock_2_out);  // AND_Gate
  not not_2 (not_2_out, control_unit_1_read[0]);
  assign control_unit_1_read[1] = not_2_out ? and_2_out : 1'bz;  // Controlled_Buffer controlled_buffer_1
  assign controlled_buffer_2_out = not_2_out ? control_unit_1_char_out : 8'bz;  // Controlled_Buffer controlled_buffer_2
  Register register_1 (
    .D(controlled_buffer_2_out), .en(control_unit_1_read[0]), .clk(control_unit_1_read[1]), .Q(register_1_q),
    .clr(RESET));
  and and_3 (and_3_out, control_unit_1_read[1], control_unit_1_read[0]);
  D_Flip_Flop d_ff_1 (.D(1'b0), .clk(clock_3_out), .Q(d_ff_1_q), .preset(and_3_out), .reset(RESET));  // open: Qn
  Clock clock_3 (.out(clock_3_out));
  not not_3 (not_3_out, control_unit_1_read[0]);
  program_storage program_storage_1 (
    .RESET(RESET), .ENABLE(or_1_out), .LOAD(jump_unit_1_jump), .ADDR_IN(jump_unit_1_addr_out),
    .DATA(program_storage_1_data), .ADDR_OUT(program_storage_1_addr_out));
  jump_unit jump_unit_1 (
    .RESET(RESET), .ENABLE(and_1_out), .ADDR_IN(program_storage_1_addr_out),
    .DATA_IN(memory_unit_1_data_out), .FORWARD(control_unit_1_forward), .BACKWARD(control_unit_1_backward),
    .ADDR_OUT(jump_unit_1_addr_out), .JUMP(jump_unit_1_jump), .OVERRIDE(jump_unit_1_override));
  and and_4 (and_4_out, d_ff_1_q, control_unit_1_read[0]);
  or or_2 (or_2_out, and_4_out, not_3_out);
  control_unit control_unit_1 (
    .PROGRAM(program_storage_1_data), .RESET(RESET), .DATA_IN(memory_unit_1_data_out),
    .CHAR_IN(register_1_q), .DIRECTION(control_unit_1_direction), .COUNT(control_unit_1_count),
    .CHAR_OUT(control_unit_1_char_out), .DATA_OUT(control_unit_1_data_out), .READ(control_unit_1_read[0]),
    .PRINT(control_unit_1_print), .WRITE(control_unit_1_write), .FORWARD(control_unit_1_forward),
    .BACKWARD(control_unit_1_backward));
  memory_unit memory_unit_1 (
    .ENABLE(and_1_out), .RESET(RESET), .DIRECTION(control_unit_1_direction), .COUNT(control_unit_1_count),
    .WRITE(control_unit_1_write), .DATA_IN(control_unit_1_data_out), .DATA_OUT(memory_unit_1_data_out));
  not not_4 (not_4_out, control_unit_1_read[0]);
  Demultiplexer #(.width(7)) demultiplexer_1 (
    .out0(demultiplexer_1_out0), .out1(demultiplexer_1_out1), .in(controlled_buffer_2_out[6:0]),
    .sel(controlled_buffer_2_out[7]));
  TTY tty_1 (.data(demultiplexer_1_out0), .clk(control_unit_1_read[1]), .we(not_4_out), .clr(RESET));
  Register #(.width(7)) register_2 (
    .D(demultiplexer_1_out1), .clk(control_unit_1_read[1]), .Q(register_2_q), .clr(RESET));  // open: en
  assign controlled_buffer_2_out = and_5_out ? {1'b0, keyboard_1_data} : 8'bz;  // Controlled_Buffer controlled_buffer_3
  assign control_unit_1_read[1] = and_5_out ? not_5_out : 1'bz;  // Controlled_Buffer controlled_buffer_4
  LED led_1 (.in(register_2_q[6]));
  LED led_2 (.in(register_2_q[5]));
  Clock clock_4 (.out(clock_4_out));
  Keyboard keyboard_1 (
    .clk(clock_4_out), .re(and_5_out), .clr(RESET), .avail(keyboard_1_avail), .data(keyboard_1_data));
  Clock clock_5 (.out(clock_5_out));
  not not_5 (not_5_out, clock_5_out);
  and and_5 (and_5_out, control_unit_1_read[0], keyboard_1_avail);
  LED led_3 (.in(register_2_q[4]));
  LED led_4 (.in(register_2_q[3]));
  LED led_5 (.in(register_2_q[2]));
  LED led_6 (.in(register_2_q[1]));
  LED led_7 (.in(register_2_q[0]));

  // Notes on the sheet:
  //   I/O unit
  //   not in actual logic
endmodule

module program_storage (
  input  RESET,
  input  ENABLE,
  input  LOAD,
  input  [14:0] ADDR_IN,
  output [7:0] DATA,
  output [14:0] ADDR_OUT
);

  wire and_1_out, clock_1_out, comparator_1_eq, not_1_out;

  not not_1 (not_1_out, comparator_1_eq);
  Comparator comparator_1 (.a(DATA), .b({8{1'b0}}), .eq(comparator_1_eq));  // open: gt, lt
  and and_1 (and_1_out, ENABLE, not_1_out);
  Clock clock_1 (.out(clock_1_out));
  Counter #(.max('h7fff), .width(15)) PC (
    .clr(RESET), .load(LOAD), .count(and_1_out), .clk(clock_1_out), .D(ADDR_IN), .Q(ADDR_OUT));  // open: up, carry
  ROM #(.addrWidth(15)) ROM_1 (.addr(ADDR_OUT), .data(DATA));

  // Notes on the sheet:
  //   contents of ROM_1 (hex, n*v repeats v):
  //   6*2b 3e 2b 2b 3c 5b 2d 3e 5b 2d 3e 2b 3e 2b 3c 3c 5d 3e 5b 2d 3c 2b 3e 5d 3e 5b 2d 3c 3c 2b 3e 3e 5d
  //   3c 3c 3c 5d 3e 5b 2b 2e 5d
endmodule

module memory_unit (
  input  ENABLE,
  input  RESET,
  input  DIRECTION,
  input  COUNT,
  input  WRITE,
  input  [7:0] DATA_IN,
  output [7:0] DATA_OUT
);

  wire and_1_out, and_2_out, clock_1_out, clock_2_out, clock_3_out, not_1_out;
  wire [14:0] CURSOR_q;

  Counter #(.max('h7fff), .width(15)) CURSOR (
    .clr(RESET), .up(DIRECTION), .count(and_1_out), .clk(clock_1_out), .Q(CURSOR_q));  // open: load, D, carry
  and and_1 (and_1_out, ENABLE, COUNT);
  Clock clock_1 (.out(clock_1_out));
  Clock clock_2 (.out(clock_2_out));
  and and_2 (and_2_out, WRITE, ENABLE, ~clock_2_out);  // AND_Gate
  RAM #(.addrWidth(15), .asyncread("true"), .clearpin("true"), .databus("bidir")) RAM_1 (
    .addr(CURSOR_q), .we(and_2_out), .oe(not_1_out), .clk(clock_3_out), .data(DATA_OUT), .clr(RESET));
  not not_1 (not_1_out, and_2_out);
  Clock clock_3 (.out(clock_3_out));
  assign DATA_OUT = and_2_out ? DATA_IN : 8'bz;  // Controlled_Buffer controlled_buffer_1
endmodule

module jump_unit (
  input  RESET,
  input  ENABLE,
  input  [14:0] ADDR_IN,
  input  [7:0] DATA_IN,
  input  FORWARD,
  input  BACKWARD,
  output [14:0] ADDR_OUT,
  output JUMP,
  output OVERRIDE
);

  wire and_1_out, and_2_out, and_4_out, and_5_out, clock_1_out, clock_2_out, clock_3_out, clock_4_out,
       comparator_1_eq, comparator_2_eq, not_1_out, not_2_out, not_3_out, or_1_out, or_2_out;
  wire [14:0] adder_1_out, counter_1_q, multiplexer_1_out, register_1_q, subtractor_1_out;

  or or_1 (or_1_out, ENABLE, OVERRIDE);
  not not_1 (not_1_out, OVERRIDE);
  Comparator comparator_1 (.a(DATA_IN), .b({8{1'b0}}), .eq(comparator_1_eq));  // open: gt, lt
  Comparator #(.width(15)) comparator_2 (.a(counter_1_q), .b(adder_1_out), .eq(comparator_2_eq));  // open: gt, lt
  Clock clock_1 (.out(clock_1_out));
  not not_2 (not_2_out, comparator_1_eq);
  and and_1 (and_1_out, or_1_out, FORWARD, not_1_out, comparator_1_eq);
  S_R_Flip_Flop s_r_ff_1 (
    .S(and_1_out), .R(and_2_out), .clk(clock_2_out), .Q(OVERRIDE), .reset(RESET));  // open: Qn, preset
  Clock clock_2 (.out(clock_2_out));
  and and_2 (and_2_out, comparator_1_eq, BACKWARD, comparator_2_eq, or_1_out);
  Register #(.width(15)) register_1 (.D(counter_1_q), .en(and_1_out), .clk(clock_1_out), .Q(register_1_q), .clr(RESET));
  and and_3 (JUMP, not_1_out, BACKWARD, not_2_out);
  Counter #(.max('h7fff), .width(15)) counter_1 (
    .clr(RESET), .up(FORWARD), .count(and_4_out), .clk(clock_3_out), .Q(counter_1_q));  // open: load, D, carry
  and and_4 (and_4_out, or_1_out, or_2_out);
  or or_2 (or_2_out, FORWARD, BACKWARD);
  Clock clock_3 (.out(clock_3_out));
  Adder #(.width(15)) adder_1 (.a(register_1_q), .b(15'h1), .out(adder_1_out));  // open: cin, cout
  assign ADDR_OUT = and_5_out ? ADDR_IN : 15'bz;  // Controlled_Buffer controlled_buffer_1
  and and_5 (and_5_out, or_1_out, FORWARD);
  Subtractor #(.width(15)) subtractor_1 (.a(counter_1_q), .b(15'h1), .out(subtractor_1_out));  // open: bin, bout
  Multiplexer #(.width(15)) multiplexer_1 (
    .in0(subtractor_1_out), .in1(counter_1_q), .out(multiplexer_1_out), .sel(and_5_out));
  not not_3 (not_3_out, and_5_out);
  Clock clock_4 (.out(clock_4_out));
  RAM #(.addrWidth(15), .asyncread("true"), .clearpin("true"), .dataWidth(15), .databus("bidir")) ram_1 (
    .addr(multiplexer_1_out), .we(and_5_out), .oe(not_3_out), .clk(clock_4_out), .data(ADDR_OUT), .clr(RESET));
endmodule

module control_unit (
  input  [7:0] PROGRAM,
  input  RESET,
  input  [7:0] DATA_IN,
  input  [7:0] CHAR_IN,
  output DIRECTION,
  output COUNT,
  output [7:0] CHAR_OUT,
  output [7:0] DATA_OUT,
  output READ,
  output PRINT,
  output WRITE,
  output FORWARD,
  output BACKWARD
);

  wire clock_1_out, clock_2_out, comparator_2_eq, comparator_3_eq, comparator_4_eq, or_2_out;
  wire [7:0] adder_1_out, register_1_q, register_2_q, subtractor_1_out;

  Comparator comparator_1 (.a(PROGRAM), .b(8'h3e), .eq(DIRECTION));  // open: gt, lt
  Comparator comparator_2 (.a(PROGRAM), .b(8'h3c), .eq(comparator_2_eq));  // open: gt, lt
  Comparator comparator_3 (.a(PROGRAM), .b(8'h2b), .eq(comparator_3_eq));  // open: gt, lt
  Comparator comparator_4 (.a(PROGRAM), .b(8'h2d), .eq(comparator_4_eq));  // open: gt, lt
  Comparator comparator_5 (.a(PROGRAM), .b(8'h2c), .eq(READ));  // open: gt, lt
  Comparator comparator_6 (.a(PROGRAM), .b(8'h2e), .eq(PRINT));  // open: gt, lt
  Comparator comparator_7 (.a(PROGRAM), .b(8'h5b), .eq(FORWARD));  // open: gt, lt
  Comparator comparator_8 (.a(PROGRAM), .b(8'h5d), .eq(BACKWARD));  // open: gt, lt
  or or_1 (COUNT, DIRECTION, comparator_2_eq);
  or or_2 (or_2_out, comparator_3_eq, comparator_4_eq);
  or or_3 (WRITE, READ, or_2_out);
  Adder adder_1 (.a(DATA_IN), .b(8'h1), .out(adder_1_out));  // open: cin, cout
  Subtractor subtractor_1 (.a(DATA_IN), .b(8'h1), .out(subtractor_1_out));  // open: bin, bout
  assign DATA_OUT = READ ? CHAR_IN : 8'bz;  // Controlled_Buffer controlled_buffer_1
  Register #(.trigger("falling")) register_1 (
    .D(adder_1_out), .clk(clock_1_out), .Q(register_1_q), .clr(RESET));  // open: en
  Clock clock_1 (.out(clock_1_out));
  Register #(.trigger("falling")) register_2 (
    .D(subtractor_1_out), .clk(clock_2_out), .Q(register_2_q), .clr(RESET));  // open: en
  Clock clock_2 (.out(clock_2_out));
  assign DATA_OUT = comparator_3_eq ? register_1_q : 8'bz;  // Controlled_Buffer controlled_buffer_2
  assign DATA_OUT = comparator_4_eq ? register_2_q : 8'bz;  // Controlled_Buffer controlled_buffer_3

  assign CHAR_OUT = DATA_IN;
endmodule

module io_unit (
  input  RESET,
  input  ENABLE,
  input  PRINT,
  input  READ,
  input  [7:0] CHAR_IN,
  input  [9:0] IO_PORT_IN,
  output [9:0] IO_PORT_OUT,
  output [7:0] CHAR_OUT,
  output HALT
);

  wire and_2_out, and_3_out, clock_1_out, clock_2_out, not_1_out, t_ff_1_q;

  and and_1 (IO_PORT_IN[1], ENABLE, PRINT, clock_1_out);
  Clock clock_1 (.out(clock_1_out));
  Register register_1 (.D(CHAR_IN), .en(IO_PORT_IN[0]), .clk(IO_PORT_IN[1]), .Q(CHAR_OUT), .clr(RESET));
  and and_2 (and_2_out, IO_PORT_IN[1], IO_PORT_IN[0]);
  T_Flip_Flop t_ff_1 (.clk(clock_2_out), .Q(t_ff_1_q), .reset(RESET), .preset(and_2_out));  // open: T, Qn
  Clock clock_2 (.out(clock_2_out));
  and and_3 (and_3_out, t_ff_1_q, IO_PORT_IN[0]);
  not not_1 (not_1_out, IO_PORT_IN[0]);
  or or_1 (HALT, and_3_out, not_1_out);

  assign IO_PORT_IN[9:2] = CHAR_IN;
  assign IO_PORT_OUT = {CHAR_IN, IO_PORT_IN[1:0]};
  assign READ = IO_PORT_IN[0];
endmodule
